# Fritzing sketch esp8266ledctl (saved by Fritzing 0.9.3b)
circuit board: 9.24293cm x 6.65104cm
breadboards: 1

parts:
  IC2 = IC, DIP package, 8 pins [chip_label=TC4420]
  IC3 = IC, DIP package, 8 pins [chip_label=TC4420]
  Q1 = MOSFET-NCHANNEL [part_number=TC4420 package=to220v]
  Q2 = MOSFET-NCHANNEL [part_number=TC4420 package=to220v]
  Q3 = MOSFET-NCHANNEL [part_number=TC4420 package=to220v]
  C1 = Ceramic Capacitor [capacitance=0.1µF package="1206 [SMD, multilayer]"]
  C2 = Ceramic Capacitor [capacitance=0.1µF package="1206 [SMD, multilayer]"]
  C3 = Ceramic Capacitor [capacitance=0.1µF package="1206 [SMD, multilayer]"]
  C4 = Electrolytic Capacitor [capacitance=10µF package="100 mil [THT, electrolytic]"]
  C5 = Electrolytic Capacitor [capacitance=10µF package="100 mil [THT, electrolytic]"]
  C6 = Electrolytic Capacitor [capacitance=10µF package="100 mil [THT, electrolytic]"]
  IC4 = Voltage Regulator [package=78xxl]
  C8 = Electrolytic Capacitor [capacitance=10µF package="100 mil [THT, electrolytic]"]
  C9 = Ceramic Capacitor [capacitance=0.1µF package="100 mil [THT, multilayer]"]
  C10 = Electrolytic Capacitor [capacitance=10µF package="100 mil [THT, electrolytic]"]
  J2_POWER_IN = Screw terminal - 2 pins [package=THT]
  J1_LED_HEADER = female pin header, 4 pins [form="♀ (female)"]
  WeMos_D1_Mini1 = WeMos D1 Mini
  IC1 = IC, DIP package, 8 pins [chip_label=TC4420]

nets (from the schematic view):
  12V: IC2.pin1, IC3.pin1, C1.1, C2.1, C3.1, C4.+, C5.+, C6.+, IC4.IN, C8.+, J2_POWER_IN.pin1, J1_LED_HEADER.pin1, IC1.pin1
  N1: IC2.pin2, WeMos_D1_Mini1.D2
  GND: IC2.pin4, IC3.pin4, Q1.S, Q2.S, Q3.S, C1.0, C2.0, C3.0, C4.-, C5.-, C6.-, IC4.GND, C8.-, C9.0, C10.-, J2_POWER_IN.pin2, WeMos_D1_Mini1.G, IC1.pin4
  N2: IC2.pin7, Q2.G
  N3: IC3.pin2, WeMos_D1_Mini1.D3
  N4: IC3.pin7, Q3.G
  N5: Q1.G, IC1.pin6
  LED_R: Q1.D
  LED_G: Q2.D
  LED_B: Q3.D
  5V: IC4.OUT, C9.1, C10.+, WeMos_D1_Mini1.5V
  etiqueta de rede: J1_LED_HEADER.pin2, J1_LED_HEADER.pin3, J1_LED_HEADER.pin4
  N6: WeMos_D1_Mini1.D1, IC1.pin2
